// Logisim project LAB 2.circ as structural Verilog
module gates (
  input  a,
  input  b,
  input  c,
  output x
);

  wire and_1_out, not_1_out, not_2_out, not_3_out;

  not not_1 (not_1_out, b);
  not not_2 (not_2_out, c);
  not not_3 (not_3_out, a);
  and and_1 (and_1_out, not_1_out, not_2_out);
  or or_1 (x, not_3_out, and_1_out);

  // Notes on the sheet:
  //   101=0
endmodule

module NAND_ONLY (
  input  a,
  input  b,
  input  c,
  output x
);

  wire nand_1_out, nand_2_out, nand_3_out;

  nand nand_1 (nand_1_out, b, b);
  nand nand_2 (nand_2_out, c, c);
  nand nand_3 (nand_3_out, nand_1_out, nand_2_out);
  nand nand_4 (x, a, nand_3_out);
endmodule
