// Logisim project Lab 3.circ as structural Verilog: 2 circuits, main circuit 33
module _33 (
  input  in_1
);

  wire and_1_out, and_2_out, and_3_out, clock_1_out, d_ff_1_q, d_ff_1_qn, d_ff_2_q, d_ff_2_qn, not_1_out,
       not_2_out, or_1_out, or_2_out;

  and and_1 (and_1_out, in_1, d_ff_2_q);
  and and_2 (and_2_out, and_1_out, not_1_out);
  and and_3 (and_3_out, d_ff_2_q, not_1_out);
  or or_1 (or_1_out, and_2_out, and_3_out);
  or or_2 (or_2_out, not_1_out, not_2_out);
  Clock clock_1 (.out(clock_1_out));
  D_Flip_Flop d_ff_1 (.clk(or_1_out), .D(clock_1_out), .Q(d_ff_1_q), .Qn(d_ff_1_qn));  // open: preset, en, reset
  D_Flip_Flop d_ff_2 (.clk(or_2_out), .D(clock_1_out), .Q(d_ff_2_q), .Qn(d_ff_2_qn));  // open: preset, en, reset
  not not_1 (not_1_out, d_ff_1_qn);
  LED led_1 (.in(d_ff_2_q));
  not not_2 (not_2_out, d_ff_2_qn);
  LED led_2 (.in(d_ff_1_q));
  LED led_3 (.in(not_1_out));
  LED led_4 (.in(not_2_out));
endmodule

module _333 (
  input  a
);

  wire clock_1_out, d_ff_1_q, d_ff_1_qn, d_ff_2_q, d_ff_2_qn, nand_1_out, nand_2_out, nand_3_out, nand_4_out,
       nand_5_out, nand_6_out, nand_7_out, nand_8_out, nand_9_out, nand_10_out, nand_11_out, nand_12_out,
       nand_13_out, nand_14_out, undriven, undriven_2, undriven_3;

  nand nand_1 (nand_1_out, a, undriven);
  nand nand_2 (nand_2_out, nand_1_out, nand_1_out);
  nand nand_3 (nand_3_out, undriven, d_ff_2_q, undriven_2, undriven_2);
  nand nand_4 (nand_4_out, nand_2_out, nand_13_out);
  nand nand_5 (nand_5_out, nand_3_out, nand_3_out);
  nand nand_6 (nand_6_out, nand_4_out, nand_4_out);
  nand nand_7 (nand_7_out, nand_5_out, nand_5_out);
  nand nand_8 (nand_8_out, undriven, undriven);
  nand nand_9 (nand_9_out, nand_14_out, nand_14_out);
  nand nand_10 (nand_10_out, nand_6_out, nand_6_out);
  nand nand_11 (nand_11_out, nand_10_out, nand_7_out);
  nand nand_12 (nand_12_out, nand_8_out, nand_9_out, undriven_3, undriven_3);
  Clock clock_1 (.out(clock_1_out));
  D_Flip_Flop d_ff_1 (.clk(nand_11_out), .D(clock_1_out), .Q(d_ff_1_q), .Qn(d_ff_1_qn));  // open: preset, en, reset
  LED led_1 (.in(d_ff_1_q));
  D_Flip_Flop d_ff_2 (.clk(nand_12_out), .D(clock_1_out), .Q(d_ff_2_q), .Qn(d_ff_2_qn));  // open: preset, en, reset
  nand nand_13 (nand_13_out, d_ff_1_qn, d_ff_1_qn);
  nand nand_14 (nand_14_out, d_ff_2_qn, d_ff_2_qn);
  LED led_2 (.in(d_ff_2_q));
  LED led_3 (.in(nand_14_out));
  LED led_4 (.in(nand_13_out));
endmodule
