// Logisim project lab 4.circ as structural Verilog
module main (
  input  in_1,
  input  in_2,
  input  in_3,
  input  in_4,
  input  in_5,
  input  in_6,
  input  in_7,
  input  in_8,
  input  in_9,
  input  in_10,
  input  in_11,
  input  in_12,
  output out_13,
  output out_14
);

  wire and_1_out, and_2_out, and_3_out, and_4_out, clock_1_out, d_ff_2_qn, or_1_out, or_2_out, or_3_out;

  and and_1 (and_1_out, in_1, in_2, in_3);
  and and_2 (and_2_out, in_4, in_5, in_6);
  and and_3 (and_3_out, in_7, in_8, in_9);
  and and_4 (and_4_out, in_10, in_11, in_12);
  or or_1 (or_1_out, and_1_out, and_2_out);
  or or_2 (or_2_out, and_3_out, and_4_out);
  or or_3 (or_3_out, or_1_out, or_2_out);
  Clock clock_1 (.out(clock_1_out));
  D_Flip_Flop d_ff_1 (.clk(clock_1_out), .D(or_3_out), .Q(out_13));  // open: Qn, preset, en, reset
  D_Flip_Flop d_ff_2 (.clk(clock_1_out), .D(d_ff_2_qn), .Q(out_14), .Qn(d_ff_2_qn));  // open: preset, en, reset
endmodule
