// Logisim project labs 4.circ as structural Verilog: 1 circuit, main circuit main
module main (
  input  in_1
);

  wire and_1_out, and_2_out, and_3_out, and_4_out, clock_1_out, d_ff_1_q, d_ff_1_qn, d_ff_2_q, d_ff_2_qn,
       not_1_out, or_1_out;

  not not_1 (not_1_out, in_1);
  and and_1 (and_1_out, in_1, d_ff_1_qn, d_ff_2_qn);
  and and_2 (and_2_out, d_ff_1_q, d_ff_2_qn, not_1_out);
  and and_3 (and_3_out, in_1, d_ff_1_q, d_ff_2_q);
  and and_4 (and_4_out, d_ff_1_qn, not_1_out, d_ff_2_q);
  or or_1 (or_1_out, and_1_out, and_2_out, and_4_out, and_3_out);
  Clock clock_1 (.out(clock_1_out));
  D_Flip_Flop d_ff_1 (.clk(clock_1_out), .D(or_1_out), .Q(d_ff_1_q), .Qn(d_ff_1_qn));  // open: preset, en, reset
  D_Flip_Flop d_ff_2 (.clk(clock_1_out), .D(d_ff_2_qn), .Q(d_ff_2_q), .Qn(d_ff_2_qn));  // open: preset, en, reset
  LED led_1 (.in(d_ff_1_q));
  LED led_2 (.in(d_ff_2_q));
endmodule
