// Logisim project circuit bad.circ as structural Verilog: 1 circuit, main circuit main
module main (
  input  in_1,
  output out_2
);

  wire clock_1_out, j_k_ff_1_q, j_k_ff_1_qn, j_k_ff_2_q, nand_1_out, nand_2_out, nand_3_out, nand_4_out,
       nand_5_out, nand_6_out, nand_7_out, nand_8_out, nand_9_out;

  nand nand_1 (nand_1_out, j_k_ff_1_qn, in_1);
  not nand_2 (nand_2_out, in_1);  // NAND_Gate
  nand nand_3 (nand_3_out, in_1, j_k_ff_1_q);
  nand nand_4 (nand_4_out, nand_2_out, nand_2_out);
  nand nand_5 (nand_5_out, nand_4_out, nand_4_out);
  nand nand_6 (nand_6_out, nand_4_out, nand_4_out);
  nand nand_7 (nand_7_out, nand_1_out, nand_5_out);
  nand nand_8 (nand_8_out, nand_6_out, nand_3_out);
  Clock clock_1 (.out(clock_1_out));
  J_K_Flip_Flop j_k_ff_1 (
    .clk(nand_7_out), .K(clock_1_out), .Q(j_k_ff_1_q), .Qn(j_k_ff_1_qn));  // open: J, preset, en, reset
  J_K_Flip_Flop j_k_ff_2 (.clk(nand_8_out), .K(clock_1_out), .Q(j_k_ff_2_q));  // open: J, Qn, preset, en, reset
  nand nand_9 (nand_9_out, j_k_ff_1_q, j_k_ff_2_q);
  nand nand_10 (out_2, nand_9_out, nand_9_out);
endmodule
