// Logisim project circuit good 1 with nand .circ as structural Verilog: 2 circuits, main circuit main
module main (
  input  in_1,
  output out_2
);

  wire and_1_out, clock_1_out, j_k_ff_1_q, j_k_ff_2_q, j_k_ff_2_qn, not_1_out, or_1_out;

  not not_1 (not_1_out, in_1);
  or or_1 (or_1_out, not_1_out, j_k_ff_2_qn);
  and and_1 (and_1_out, j_k_ff_1_q, in_1);
  Clock clock_1 (.out(clock_1_out));
  J_K_Flip_Flop j_k_ff_1 (.J(in_1), .clk(clock_1_out), .K(or_1_out), .Q(j_k_ff_1_q));  // open: Qn, preset, en, reset
  J_K_Flip_Flop j_k_ff_2 (
    .J(and_1_out), .clk(clock_1_out), .K(not_1_out), .Q(j_k_ff_2_q), .Qn(j_k_ff_2_qn));  // open: preset, en, reset
  and and_2 (out_2, j_k_ff_1_q, j_k_ff_2_q);
endmodule

module NAND (
  input  in_1,
  output out_2
);

  wire clock_1_out, j_k_ff_1_q, j_k_ff_2_q, j_k_ff_2_qn, nand_1_out, nand_2_out, nand_3_out, nand_4_out,
       nand_5_out, nand_6_out, nand_7_out;

  nand nand_1 (nand_1_out, in_1, in_1);
  nand nand_2 (nand_2_out, j_k_ff_1_q, in_1);
  nand nand_3 (nand_3_out, j_k_ff_2_qn, j_k_ff_2_qn);
  nand nand_4 (nand_4_out, nand_1_out, nand_1_out);
  nand nand_5 (nand_5_out, nand_2_out, nand_2_out);
  nand nand_6 (nand_6_out, nand_4_out, nand_3_out);
  Clock clock_1 (.out(clock_1_out));
  J_K_Flip_Flop j_k_ff_1 (.J(in_1), .clk(clock_1_out), .K(nand_6_out), .Q(j_k_ff_1_q));  // open: Qn, preset, en, reset
  J_K_Flip_Flop j_k_ff_2 (
    .J(nand_5_out), .clk(clock_1_out), .K(nand_1_out), .Q(j_k_ff_2_q), .Qn(j_k_ff_2_qn));  // open: preset, en, reset
  nand nand_7 (nand_7_out, j_k_ff_1_q, j_k_ff_2_q);
  nand nand_8 (out_2, nand_7_out, nand_7_out);
endmodule
